// Logisim project contador.circ as structural Verilog
module contatodr_sinc_0a15 (
  input  in_1,
  input  in_2,
  output Q3,
  output Q2,
  output Q1,
  output Q0
);

  wire controle_0a15_1_d0, controle_0a15_1_d1, controle_0a15_1_d2, controle_0a15_1_d3;

  D_Flip_Flop D3 (.clk(in_1), .D(controle_0a15_1_d3), .Q(Q3), .reset(in_2));  // open: Qn, preset, en
  D_Flip_Flop D2 (.clk(in_1), .D(controle_0a15_1_d2), .Q(Q2), .reset(in_2));  // open: Qn, preset, en
  D_Flip_Flop D1 (.clk(in_1), .D(controle_0a15_1_d1), .Q(Q1), .reset(in_2));  // open: Qn, preset, en
  Controle_0a15 controle_0a15_1 (
    .Q3(Q3), .Q2(Q2), .Q1(Q1), .Q0(Q0), .D3(controle_0a15_1_d3), .D2(controle_0a15_1_d2),
    .D1(controle_0a15_1_d1), .D0(controle_0a15_1_d0));
  D_Flip_Flop D0 (.clk(in_1), .D(controle_0a15_1_d0), .Q(Q0), .reset(in_2));  // open: Qn, preset, en
endmodule

module Controle_0a15 (
  input  Q3,
  input  Q2,
  input  Q1,
  input  Q0,
  output D3,
  output D2,
  output D1,
  output D0
);

  wire and_1_out, and_2_out, and_3_out, and_4_out, and_5_out, and_6_out, and_7_out, and_8_out, and_9_out,
       not_1_out, not_2_out, not_3_out, not_4_out, not_5_out, not_6_out, not_7_out, not_8_out, not_9_out;

  not not_1 (not_1_out, Q3);
  not not_2 (not_2_out, Q2);
  not not_3 (not_3_out, Q1);
  not not_4 (not_4_out, Q0);
  not not_5 (not_5_out, Q2);
  and and_1 (and_1_out, not_5_out, Q1, Q0);
  and and_2 (and_2_out, Q2, not_6_out);
  not not_6 (not_6_out, Q1);
  and and_3 (and_3_out, Q2, not_7_out);
  not not_7 (not_7_out, Q0);
  not not_8 (not_8_out, Q1);
  and and_4 (and_4_out, not_8_out, Q0);
  and and_5 (and_5_out, Q1, not_9_out);
  not not_9 (not_9_out, Q0);
  not not_10 (D0, Q0);
  and and_6 (and_6_out, not_1_out, Q2, Q1, Q0);
  and and_7 (and_7_out, Q3, not_2_out);
  and and_8 (and_8_out, Q3, not_3_out);
  and and_9 (and_9_out, Q3, not_4_out);
  or or_1 (D2, and_1_out, and_2_out, and_3_out);
  or or_2 (D1, and_4_out, and_5_out);
  or or_3 (D3, and_6_out, and_7_out, and_8_out, and_9_out);
endmodule
