// Logisim project banco_registrador.circ as structural Verilog: 3 circuits, main circuit banco_registrador
module banco_registrador (
  input  CLK,
  input  RE,
  input  WE,
  input  ADRL,
  input  in_5,
  input  [7:0] D,
  output [7:0] out_7
);

  wire and_1_out, dmplex_1_out_4, dmplex_1_out_5, dmplex_1_out_6, dmplex_1_out_7;
  wire [7:0] cregister_1_do;

  and and_1 (and_1_out, WE, CLK);
  dmplex dmplex_1 (
    .D(CLK), .SL(ADRL), .SH(in_5), .out_4(dmplex_1_out_4), .out_5(dmplex_1_out_5), .out_6(dmplex_1_out_6),
    .out_7(dmplex_1_out_7));
  assign out_7 = RE ? cregister_1_do : 8'bz;  // Controlled_Buffer controlled_buffer_1
  cregister cregister_1 (.CLK(dmplex_1_out_4), .E(and_1_out), .Di(D), .Do(cregister_1_do));
  cregister cregister_2 (.CLK(dmplex_1_out_5), .E(and_1_out), .Di(D), .Do(cregister_1_do));
  cregister cregister_3 (.CLK(dmplex_1_out_6), .E(and_1_out), .Di(D), .Do(cregister_1_do));
  cregister cregister_4 (.CLK(dmplex_1_out_7), .E(and_1_out), .Di(D), .Do(cregister_1_do));
endmodule

module dmplex (
  input  D,
  input  SL,
  input  SH,
  output out_4,
  output out_5,
  output out_6,
  output out_7
);

  wire and_1_out, and_2_out, and_3_out, and_4_out, not_1_out, not_2_out;

  not not_1 (not_1_out, SH);
  not not_2 (not_2_out, SL);
  and and_1 (and_1_out, not_2_out, not_1_out);
  and and_2 (and_2_out, SL, not_1_out);
  and and_3 (and_3_out, not_2_out, SH);
  and and_4 (and_4_out, SL, SH);
  and and_5 (out_4, D, and_1_out);
  and and_6 (out_5, D, and_2_out);
  and and_7 (out_6, D, and_3_out);
  and and_8 (out_7, D, and_4_out);
endmodule

module cregister (
  input  CLK,
  input  E,
  input  [7:0] Di,
  output [7:0] Do
);

  wire and_1_out;
  wire [7:0] register8s_1_out_3;

  and and_1 (and_1_out, CLK, E);
  register8s register8s_1 (.CLK(and_1_out), .in_2(Di), .out_3(register8s_1_out_3));
  assign Do = CLK ? register8s_1_out_3 : 8'bz;  // Controlled_Buffer controlled_buffer_1
endmodule
