// Logisim project flipflop.circ as structural Verilog: 4 circuits, main circuit ffd
module latch (
  input  in_1,
  input  in_2,
  output out_3,
  output out_4
);

  or or_1 (out_3, ~in_1, ~out_4);  // OR_Gate
  or or_2 (out_4, ~out_3, ~in_2);  // OR_Gate
endmodule

module ffsr (
  input  S,
  input  CLK,
  input  R,
  output out_4,
  output out_5
);

  wire nand_1_out, nand_2_out;

  nand nand_1 (nand_1_out, S, CLK);
  nand nand_2 (nand_2_out, CLK, R);
  latch latch_1 (.in_1(nand_1_out), .in_2(nand_2_out), .out_3(out_4), .out_4(out_5));
endmodule

module ffjk (
  input  in_1,
  input  in_2,
  input  in_3
);

  wire nand_1_out, nand_2_out, nand_3_out, nand_4_out, nand_5_out, nand_6_out, nand_7_out, nand_8_out,
       not_1_out;

  nand nand_1 (nand_1_out, nand_8_out, in_1, in_2);
  nand nand_2 (nand_2_out, in_2, in_3, nand_7_out);
  nand nand_3 (nand_3_out, nand_1_out, nand_4_out);
  nand nand_4 (nand_4_out, nand_3_out, nand_2_out);
  not not_1 (not_1_out, in_2);
  nand nand_5 (nand_5_out, nand_3_out, not_1_out);
  nand nand_6 (nand_6_out, not_1_out, nand_4_out);
  nand nand_7 (nand_7_out, nand_5_out, nand_8_out);
  nand nand_8 (nand_8_out, nand_7_out, nand_6_out);
endmodule

module ffd (
  input  D,
  input  CLK,
  output out_3
);

  wire ffsr_1_out_4, ffsr_1_out_5, not_1_out, not_2_out;

  not not_1 (not_1_out, D);
  not not_2 (not_2_out, CLK);
  ffsr ffsr_1 (.S(D), .CLK(CLK), .R(not_1_out), .out_4(ffsr_1_out_4), .out_5(ffsr_1_out_5));
  ffsr ffsr_2 (.S(ffsr_1_out_4), .CLK(not_2_out), .R(ffsr_1_out_5), .out_4(out_3));  // open: out_5
endmodule
