// Logisim project memoria.circ as structural Verilog: 2 circuits, main circuit register8
module register8 (
  input  CLK,
  input  in_2,
  input  in_3,
  input  in_4,
  input  in_5,
  input  in_6,
  input  in_7,
  input  in_8,
  input  in_9,
  output out_10,
  output out_11,
  output out_12,
  output out_13,
  output out_14,
  output out_15,
  output out_16,
  output out_17
);

  ffd ffd_1 (.D(in_2), .CLK(CLK), .out_3(out_10));
  ffd ffd_2 (.D(in_3), .CLK(CLK), .out_3(out_11));
  ffd ffd_3 (.D(in_4), .CLK(CLK), .out_3(out_12));
  ffd ffd_4 (.D(in_5), .CLK(CLK), .out_3(out_13));
  ffd ffd_5 (.D(in_6), .CLK(CLK), .out_3(out_14));
  ffd ffd_6 (.D(in_7), .CLK(CLK), .out_3(out_15));
  ffd ffd_7 (.D(in_8), .CLK(CLK), .out_3(out_16));
  ffd ffd_8 (.D(in_9), .CLK(CLK), .out_3(out_17));
endmodule

module register8s (
  input  CLK,
  input  [7:0] in_2,
  output [7:0] out_3
);

  register8 register8_1 (
    .CLK(CLK), .in_2(in_2[0]), .in_3(in_2[1]), .in_4(in_2[2]), .in_5(in_2[3]), .in_6(in_2[4]),
    .in_7(in_2[5]), .in_8(in_2[6]), .in_9(in_2[7]), .out_10(out_3[0]), .out_11(out_3[1]), .out_12(out_3[2]),
    .out_13(out_3[3]), .out_14(out_3[4]), .out_15(out_3[5]), .out_16(out_3[6]), .out_17(out_3[7]));
endmodule
