// Logisim project multiplex.circ as structural Verilog: 6 circuits, main circuit mplex2
module mplex1 (
  input  in_1,
  input  in_2,
  input  SLK,
  output out_4
);

  wire and_1_out, and_2_out;

  and and_1 (and_1_out, in_1, ~SLK);  // AND_Gate
  and and_2 (and_2_out, in_2, SLK);
  or or_1 (out_4, and_1_out, and_2_out);
endmodule

module mplex2 (
  input  in_1,
  input  in_2,
  input  in_3,
  input  in_4,
  input  SL,
  input  SH,
  output out_7
);

  wire mplex1_1_out_4, mplex1_2_out_4;

  mplex1 mplex1_1 (.in_1(in_1), .in_2(in_2), .SLK(SL), .out_4(mplex1_1_out_4));
  mplex1 mplex1_2 (.in_1(in_3), .in_2(in_4), .SLK(SL), .out_4(mplex1_2_out_4));
  mplex1 mplex1_3 (.in_1(mplex1_1_out_4), .in_2(mplex1_2_out_4), .SLK(SH), .out_4(out_7));
endmodule

module mplex1d8 (
  input  S,
  input  [7:0] in_2,
  input  [7:0] in_3,
  output [7:0] out_4
);

  wire not_1_out;

  not not_1 (not_1_out, S);
  assign out_4 = not_1_out ? in_2 : 8'bz;  // Controlled_Buffer controlled_buffer_1
  assign out_4 = S ? in_3 : 8'bz;  // Controlled_Buffer controlled_buffer_2
endmodule

module mplex2d8 (
  input  Sl,
  input  Sh,
  input  [7:0] in_3,
  input  [7:0] in_4,
  input  [7:0] in_5,
  input  [7:0] in_6,
  output [7:0] out_7
);

  wire [7:0] mplex1d8_1_out_4, mplex1d8_2_out_4;

  mplex1d8 mplex1d8_1 (.S(Sl), .in_2(in_3), .in_3(in_4), .out_4(mplex1d8_1_out_4));
  mplex1d8 mplex1d8_2 (.S(Sl), .in_2(in_5), .in_3(in_6), .out_4(mplex1d8_2_out_4));
  mplex1d8 mplex1d8_3 (.S(Sh), .in_2(mplex1d8_1_out_4), .in_3(mplex1d8_2_out_4), .out_4(out_7));
endmodule

module mplex3d8 (
  input  Sl,
  input  in_2,
  input  Sh,
  input  [7:0] in_4,
  input  [7:0] in_5,
  input  [7:0] in_6,
  input  [7:0] in_7,
  input  [7:0] in_8,
  input  [7:0] in_9,
  input  [7:0] in_10,
  input  [7:0] in_11,
  output [7:0] out_12
);

  wire [7:0] mplex2d8_1_out_7, mplex2d8_2_out_7;

  mplex2d8 mplex2d8_1 (
    .Sl(Sl), .Sh(in_2), .in_3(in_4), .in_4(in_5), .in_5(in_6), .in_6(in_7), .out_7(mplex2d8_1_out_7));
  mplex2d8 mplex2d8_2 (
    .Sl(Sl), .Sh(in_2), .in_3(in_8), .in_4(in_9), .in_5(in_10), .in_6(in_11), .out_7(mplex2d8_2_out_7));
  mplex1d8 mplex1d8_1 (.S(Sh), .in_2(mplex2d8_1_out_7), .in_3(mplex2d8_2_out_7), .out_4(out_12));
endmodule

module mplex4d8 (
  input  [3:0] S,
  input  [7:0] in_2,
  input  [7:0] in_3,
  input  [7:0] in_4,
  input  [7:0] in_5,
  input  [7:0] in_6,
  input  [7:0] in_7,
  input  [7:0] in_8,
  input  [7:0] in_9,
  input  [7:0] in_10,
  input  [7:0] in_11,
  input  [7:0] in_12,
  input  [7:0] in_13,
  input  [7:0] in_14,
  input  [7:0] in_15,
  input  [7:0] in_16,
  input  [7:0] in_17,
  output [7:0] out_18
);

  wire [7:0] mplex3d8_1_out_12, mplex3d8_2_out_12;

  mplex3d8 mplex3d8_1 (
    .Sl(S[0]), .in_2(S[1]), .Sh(S[2]), .in_4(in_2), .in_5(in_3), .in_6(in_4), .in_7(in_5), .in_8(in_6),
    .in_9(in_7), .in_10(in_8), .in_11(in_9), .out_12(mplex3d8_1_out_12));
  mplex3d8 mplex3d8_2 (
    .Sl(S[0]), .in_2(S[1]), .Sh(S[2]), .in_4(in_10), .in_5(in_11), .in_6(in_12), .in_7(in_13), .in_8(in_14),
    .in_9(in_15), .in_10(in_16), .in_11(in_17), .out_12(mplex3d8_2_out_12));
  mplex1d8 mplex1d8_1 (.S(S[3]), .in_2(mplex3d8_1_out_12), .in_3(mplex3d8_2_out_12), .out_4(out_18));
endmodule
