// Logisim project extensor.circ as structural Verilog: 2 circuits, main circuit extensor
module extensor (
  input  in_1,
  input  in_2,
  input  in_3,
  input  in_4,
  output out_5,
  output out_6,
  output out_7,
  output out_8,
  output out_9,
  output out_10,
  output out_11,
  output out_12
);


  assign out_5 = in_1;
  assign out_6 = in_2;
  assign out_7 = in_3;
  assign out_8 = in_4;
  assign out_9 = in_4;
  assign out_10 = in_4;
  assign out_11 = in_4;
  assign out_12 = in_4;
endmodule

module main (
  input  in_1,
  input  in_2,
  input  in_3,
  input  in_4,
  output [7:0] out_5
);

  extensor extensor_1 (
    .in_1(in_1), .in_2(in_2), .in_3(in_3), .in_4(in_4), .out_5(out_5[0]), .out_6(out_5[1]), .out_7(out_5[2]),
    .out_8(out_5[3]), .out_9(out_5[4]), .out_10(out_5[5]), .out_11(out_5[6]), .out_12(out_5[7]));
endmodule
