// Logisim project flip_flop.circ as structural Verilog: 1 circuit, main circuit main
module main (
  input  CLK,
  input  in_2,
  input  in_3,
  input  in_4,
  input  in_5,
  input  in_6,
  input  in_7,
  input  in_8,
  input  in_9,
  output out_10,
  output out_11,
  output out_12,
  output out_13,
  output out_14,
  output out_15,
  output out_16,
  output out_17
);

  ffd ffd_1 (.D(in_2), .CLK(CLK), .out_3(out_10));
  ffd ffd_2 (.D(in_3), .CLK(CLK), .out_3(out_11));
  ffd ffd_3 (.D(in_4), .CLK(CLK), .out_3(out_12));
  ffd ffd_4 (.D(in_5), .CLK(CLK), .out_3(out_13));
  ffd ffd_5 (.D(in_6), .CLK(CLK), .out_3(out_14));
  ffd ffd_6 (.D(in_7), .CLK(CLK), .out_3(out_15));
  ffd ffd_7 (.D(in_8), .CLK(CLK), .out_3(out_16));
  ffd ffd_8 (.D(in_9), .CLK(CLK), .out_3(out_17));
endmodule
