// Logisim project alert111.circ as structural Verilog: 1 circuit, main circuit main
module main (
  input  in_1,
  input  CLK,
  output out_3
);

  wire and_1_out, and_2_out, ffd_1_out_3, ffd_2_out_3;

  and and_1 (and_1_out, in_1, CLK);
  ffd ffd_1 (.D(in_1), .CLK(CLK), .out_3(ffd_1_out_3));
  ffd ffd_2 (.D(ffd_1_out_3), .CLK(CLK), .out_3(ffd_2_out_3));
  and and_2 (and_2_out, ffd_2_out_3, and_1_out);
  and and_3 (out_3, ffd_1_out_3, and_2_out);
endmodule
