// Logisim project paridade.circ as structural Verilog: 3 circuits, main circuit paridade_impar8
module paridade_impar2 (
  input  in_1,
  input  in_2,
  output out_3
);

  wire and_1_out, and_2_out;

  and and_1 (and_1_out, ~in_1, in_2);  // AND_Gate
  and and_2 (and_2_out, in_1, ~in_2);  // AND_Gate
  or or_1 (out_3, and_1_out, and_2_out);
endmodule

module paridade_impar4 (
  input  in_1,
  input  in_2,
  input  in_3,
  input  in_4,
  output out_5
);

  wire paridade_impar2_1_out_3, paridade_impar2_2_out_3;

  paridade_impar2 paridade_impar2_1 (.in_1(in_1), .in_2(in_2), .out_3(paridade_impar2_1_out_3));
  paridade_impar2 paridade_impar2_2 (.in_1(in_3), .in_2(in_4), .out_3(paridade_impar2_2_out_3));
  paridade_impar2 paridade_impar2_3 (.in_1(paridade_impar2_1_out_3), .in_2(paridade_impar2_2_out_3), .out_3(out_5));
endmodule

module paridade_impar8 (
  input  in_1,
  input  in_2,
  input  in_3,
  input  in_4,
  input  in_5,
  input  in_6,
  input  in_7,
  input  in_8,
  output out_9
);

  wire paridade_impar4_1_out_5, paridade_impar4_2_out_5;

  paridade_impar4 paridade_impar4_1 (
    .in_1(in_1), .in_2(in_2), .in_3(in_3), .in_4(in_4), .out_5(paridade_impar4_1_out_5));
  paridade_impar4 paridade_impar4_2 (
    .in_1(in_5), .in_2(in_6), .in_3(in_7), .in_4(in_8), .out_5(paridade_impar4_2_out_5));
  paridade_impar2 paridade_impar2_1 (.in_1(paridade_impar4_1_out_5), .in_2(paridade_impar4_2_out_5), .out_3(out_9));
endmodule
