// Logisim project primos.circ as structural Verilog: 1 circuit, main circuit primos
module primos (
  input  BL,
  input  in_2,
  input  in_3,
  input  BH,
  output out_5
);

  wire and_1_out, and_2_out, and_3_out, and_4_out, and_5_out, and_6_out, and_7_out, and_8_out, not_1_out,
       not_2_out, not_3_out, or_1_out, or_2_out;

  not not_1 (not_1_out, in_2);
  not not_2 (not_2_out, in_3);
  not not_3 (not_3_out, BH);
  and and_1 (and_1_out, in_3, not_1_out);
  and and_2 (and_2_out, not_2_out, in_2);
  and and_3 (and_3_out, not_3_out, in_2);
  and and_4 (and_4_out, not_3_out, not_2_out);
  and and_5 (and_5_out, and_1_out, BL);
  and and_6 (and_6_out, and_2_out, BL);
  and and_7 (and_7_out, and_3_out, BL);
  and and_8 (and_8_out, and_4_out, in_2);
  or or_1 (or_1_out, and_5_out, and_6_out);
  or or_2 (or_2_out, or_1_out, and_7_out);
  or or_3 (out_5, or_2_out, and_8_out);
endmodule
