// Logisim project lab_ram.circ as structural Verilog: 3 circuits, main circuit lab_ram
module lab_ram (
  input  [7:0] Di,
  input  CS,
  input  RW,
  input  [3:0] ADR,
  output [7:0] Do
);

  wire and_1_out, and_2_out, line_dec_1_out_3, line_dec_1_out_4, line_dec_1_out_5, line_dec_1_out_6,
       line_dec_2_out_3, line_dec_2_out_4, line_dec_2_out_5, line_dec_2_out_6;
  wire [7:0] ram_register_1_o;

  and and_1 (and_1_out, CS, RW);
  and and_2 (and_2_out, CS, ~RW);  // AND_Gate
  line_dec line_dec_1 (
    .SL(ADR[0]), .SH(ADR[1]), .out_3(line_dec_1_out_3), .out_4(line_dec_1_out_4), .out_5(line_dec_1_out_5),
    .out_6(line_dec_1_out_6));
  line_dec line_dec_2 (
    .SL(ADR[2]), .SH(ADR[3]), .out_3(line_dec_2_out_3), .out_4(line_dec_2_out_4), .out_5(line_dec_2_out_5),
    .out_6(line_dec_2_out_6));
  ram_register ram_register_1 (
    .D(Di), .RE(line_dec_1_out_3), .CE(line_dec_2_out_3), .RW(and_1_out), .O(ram_register_1_o));
  ram_register ram_register_2 (
    .D(Di), .RE(line_dec_1_out_4), .CE(line_dec_2_out_3), .RW(and_1_out), .O(ram_register_1_o));
  ram_register ram_register_3 (
    .D(Di), .RE(line_dec_1_out_5), .CE(line_dec_2_out_3), .RW(and_1_out), .O(ram_register_1_o));
  ram_register ram_register_4 (
    .D(Di), .RE(line_dec_1_out_6), .CE(line_dec_2_out_3), .RW(and_1_out), .O(ram_register_1_o));
  ram_register ram_register_5 (
    .D(Di), .RE(line_dec_1_out_3), .CE(line_dec_2_out_4), .RW(and_1_out), .O(ram_register_1_o));
  ram_register ram_register_6 (
    .D(Di), .RE(line_dec_1_out_4), .CE(line_dec_2_out_4), .RW(and_1_out), .O(ram_register_1_o));
  ram_register ram_register_7 (
    .D(Di), .RE(line_dec_1_out_5), .CE(line_dec_2_out_4), .RW(and_1_out), .O(ram_register_1_o));
  ram_register ram_register_8 (
    .D(Di), .RE(line_dec_1_out_6), .CE(line_dec_2_out_4), .RW(and_1_out), .O(ram_register_1_o));
  assign Do = and_2_out ? ram_register_1_o : 8'bz;  // Controlled_Buffer controlled_buffer_1
  ram_register ram_register_9 (
    .D(Di), .RE(line_dec_1_out_3), .CE(line_dec_2_out_5), .RW(and_1_out), .O(ram_register_1_o));
  ram_register ram_register_10 (
    .D(Di), .RE(line_dec_1_out_4), .CE(line_dec_2_out_5), .RW(and_1_out), .O(ram_register_1_o));
  ram_register ram_register_11 (
    .D(Di), .RE(line_dec_1_out_5), .CE(line_dec_2_out_5), .RW(and_1_out), .O(ram_register_1_o));
  ram_register ram_register_12 (
    .D(Di), .RE(line_dec_1_out_6), .CE(line_dec_2_out_5), .RW(and_1_out), .O(ram_register_1_o));
  ram_register ram_register_13 (
    .D(Di), .RE(line_dec_1_out_3), .CE(line_dec_2_out_6), .RW(and_1_out), .O(ram_register_1_o));
  ram_register ram_register_14 (
    .D(Di), .RE(line_dec_1_out_4), .CE(line_dec_2_out_6), .RW(and_1_out), .O(ram_register_1_o));
  ram_register ram_register_15 (
    .D(Di), .RE(line_dec_1_out_5), .CE(line_dec_2_out_6), .RW(and_1_out), .O(ram_register_1_o));
  ram_register ram_register_16 (
    .D(Di), .RE(line_dec_1_out_6), .CE(line_dec_2_out_6), .RW(and_1_out), .O(ram_register_1_o));
endmodule

module ram_register (
  input  RE,
  input  CE,
  input  RW,
  input  [7:0] D,
  output [7:0] O
);

  wire and_1_out, and_2_out, and_3_out;
  wire [7:0] register8s_1_out_3;

  and and_1 (and_1_out, RE, CE);
  and and_2 (and_2_out, RW, and_1_out);
  and and_3 (and_3_out, ~RW, and_1_out);  // AND_Gate
  assign O = and_3_out ? register8s_1_out_3 : 8'bz;  // Controlled_Buffer controlled_buffer_1
  register8s register8s_1 (.CLK(and_2_out), .in_2(D), .out_3(register8s_1_out_3));
endmodule

module line_dec (
  input  SL,
  input  SH,
  output out_3,
  output out_4,
  output out_5,
  output out_6
);

  wire not_1_out, not_2_out;

  not not_1 (not_1_out, SL);
  not not_2 (not_2_out, SH);
  and and_1 (out_3, not_1_out, not_2_out);
  and and_2 (out_4, SL, not_2_out);
  and and_3 (out_5, not_1_out, SH);
  and and_4 (out_6, SL, SH);
endmodule
