// Logisim project lab_rom.circ as structural Verilog: 5 circuits, main circuit lab_rom
module lab_rom (
  input  [3:0] ADR,
  input  OE,
  output [7:0] out_3
);

  wire line_dec_1_out_3, line_dec_1_out_4, line_dec_1_out_5, line_dec_1_out_6, line_dec_2_out_3,
       line_dec_2_out_4, line_dec_2_out_5, line_dec_2_out_6;
  wire [7:0] rom_register_1_o;

  line_dec line_dec_1 (
    .SL(ADR[0]), .SH(ADR[1]), .out_3(line_dec_1_out_3), .out_4(line_dec_1_out_4), .out_5(line_dec_1_out_5),
    .out_6(line_dec_1_out_6));
  line_dec line_dec_2 (
    .SL(ADR[2]), .SH(ADR[3]), .out_3(line_dec_2_out_3), .out_4(line_dec_2_out_4), .out_5(line_dec_2_out_5),
    .out_6(line_dec_2_out_6));
  rom_register rom_register_1 (.D({8{1'b0}}), .RE(line_dec_1_out_3), .CE(line_dec_2_out_3), .O(rom_register_1_o));
  rom_register rom_register_2 (.D(8'h4), .RE(line_dec_1_out_4), .CE(line_dec_2_out_3), .O(rom_register_1_o));
  rom_register rom_register_3 (.D(8'h8), .RE(line_dec_1_out_5), .CE(line_dec_2_out_3), .O(rom_register_1_o));
  rom_register rom_register_4 (.D(8'hc), .RE(line_dec_1_out_6), .CE(line_dec_2_out_3), .O(rom_register_1_o));
  rom_register rom_register_5 (.D(8'h1), .RE(line_dec_1_out_3), .CE(line_dec_2_out_4), .O(rom_register_1_o));
  rom_register rom_register_6 (.D(8'h5), .RE(line_dec_1_out_4), .CE(line_dec_2_out_4), .O(rom_register_1_o));
  rom_register rom_register_7 (.D(8'h9), .RE(line_dec_1_out_5), .CE(line_dec_2_out_4), .O(rom_register_1_o));
  rom_register rom_register_8 (.D(8'hd), .RE(line_dec_1_out_6), .CE(line_dec_2_out_4), .O(rom_register_1_o));
  output_buffer output_buffer_1 (.OE(OE), .D(rom_register_1_o), .out_3(out_3));
  rom_register rom_register_9 (.D(8'h2), .RE(line_dec_1_out_3), .CE(line_dec_2_out_5), .O(rom_register_1_o));
  rom_register rom_register_10 (.D(8'h6), .RE(line_dec_1_out_4), .CE(line_dec_2_out_5), .O(rom_register_1_o));
  rom_register rom_register_11 (.D(8'ha), .RE(line_dec_1_out_5), .CE(line_dec_2_out_5), .O(rom_register_1_o));
  rom_register rom_register_12 (.D(8'he), .RE(line_dec_1_out_6), .CE(line_dec_2_out_5), .O(rom_register_1_o));
  rom_register rom_register_13 (.D(8'h3), .RE(line_dec_1_out_3), .CE(line_dec_2_out_6), .O(rom_register_1_o));
  rom_register rom_register_14 (.D(8'h7), .RE(line_dec_1_out_4), .CE(line_dec_2_out_6), .O(rom_register_1_o));
  rom_register rom_register_15 (.D(8'hb), .RE(line_dec_1_out_5), .CE(line_dec_2_out_6), .O(rom_register_1_o));
  rom_register rom_register_16 (.D(8'hf), .RE(line_dec_1_out_6), .CE(line_dec_2_out_6), .O(rom_register_1_o));
endmodule

module rom_cell (
  input  in_1,
  input  D,
  output out_3
);

  Transistor #(.\type ("n")) transistor_1 (.in(D), .out(out_3), .gate(in_1));
endmodule

module rom_register (
  input  RE,
  input  CE,
  input  [7:0] D,
  output [7:0] O
);

  wire and_1_out;

  and and_1 (and_1_out, RE, CE);
  rom_cell rom_cell_1 (.D(D[0]), .in_1(and_1_out), .out_3(O[0]));
  rom_cell rom_cell_2 (.D(D[1]), .in_1(and_1_out), .out_3(O[1]));
  rom_cell rom_cell_3 (.D(D[2]), .in_1(and_1_out), .out_3(O[2]));
  rom_cell rom_cell_4 (.D(D[3]), .in_1(and_1_out), .out_3(O[3]));
  rom_cell rom_cell_5 (.D(D[4]), .in_1(and_1_out), .out_3(O[4]));
  rom_cell rom_cell_6 (.D(D[5]), .in_1(and_1_out), .out_3(O[5]));
  rom_cell rom_cell_7 (.D(D[6]), .in_1(and_1_out), .out_3(O[6]));
  rom_cell rom_cell_8 (.D(D[7]), .in_1(and_1_out), .out_3(O[7]));
endmodule

module line_dec (
  input  SL,
  input  SH,
  output out_3,
  output out_4,
  output out_5,
  output out_6
);

  wire not_1_out, not_2_out;

  not not_1 (not_1_out, SL);
  not not_2 (not_2_out, SH);
  and and_1 (out_3, not_1_out, not_2_out);
  and and_2 (out_4, SL, not_2_out);
  and and_3 (out_5, not_1_out, SH);
  and and_4 (out_6, SL, SH);
endmodule

module output_buffer (
  input  OE,
  input  [7:0] D,
  output [7:0] out_3
);

  Pull_Resistor #(.pull(1)) pull_resistor_1 (.node(D[7]));
  Pull_Resistor #(.pull(1)) pull_resistor_2 (.node(D[6]));
  Pull_Resistor #(.pull(1)) pull_resistor_3 (.node(D[5]));
  Pull_Resistor #(.pull(1)) pull_resistor_4 (.node(D[4]));
  Pull_Resistor #(.pull(1)) pull_resistor_5 (.node(D[3]));
  Pull_Resistor #(.pull(1)) pull_resistor_6 (.node(D[2]));
  Pull_Resistor #(.pull(1)) pull_resistor_7 (.node(D[1]));
  assign out_3 = OE ? D : 8'bz;  // Controlled_Buffer controlled_buffer_1
  Pull_Resistor #(.pull(1)) pull_resistor_8 (.node(D[0]));
endmodule
