// Logisim project seq101.circ as structural Verilog: 1 circuit, main circuit seq101
module seq101 (
  input  S,
  input  CLK,
  output out_3
);

  wire and_1_out, ffd_1_out_3, ffd_2_out_3;

  ffd ffd_1 (.D(S), .CLK(CLK), .out_3(ffd_1_out_3));
  and and_1 (and_1_out, ffd_1_out_3, ~S);  // AND_Gate
  ffd ffd_2 (.D(and_1_out), .CLK(CLK), .out_3(ffd_2_out_3));
  and and_2 (out_3, ffd_2_out_3, S);
endmodule
