// Logisim project soma_4.circ as structural Verilog: 1 circuit, main circuit soma_4
module soma_4 (
  input  in_1,
  input  in_2,
  input  in_3,
  input  in_4,
  input  in_5,
  input  in_6,
  input  in_7,
  input  in_8,
  output out_9,
  output out_10,
  output out_11,
  output out_12,
  output out_13,
  output out_14,
  output out_15,
  output out_16
);

  wire add1_1_out_4, add1_2_out_4, add1_3_out_4, add1_4_out_4, add1_5_out_4;

  add1 add1_1 (.in_1(1'b1), .in_2(in_3), .out_3(out_11), .out_4(add1_1_out_4));
  add1 add1_2 (.in_1(add1_1_out_4), .in_2(in_4), .out_3(out_12), .out_4(add1_2_out_4));
  add1 add1_3 (.in_1(add1_2_out_4), .in_2(in_5), .out_3(out_13), .out_4(add1_3_out_4));
  add1 add1_4 (.in_1(add1_3_out_4), .in_2(in_6), .out_3(out_14), .out_4(add1_4_out_4));
  add1 add1_5 (.in_1(add1_4_out_4), .in_2(in_7), .out_3(out_15), .out_4(add1_5_out_4));
  add1 add1_6 (.in_1(add1_5_out_4), .in_2(in_8), .out_3(out_16));  // open: out_4

  assign out_9 = in_1;
  assign out_10 = in_2;
endmodule
