// Logisim project ula.circ as structural Verilog: 3 circuits, main circuit main
module main (
  input  [3:0] Ctrl,
  input  Cin,
  input  [7:0] A,
  input  [7:0] B,
  output [7:0] out_5,
  output Co
);

  wire [7:0] addsub_1_sub, addsub_1_sum, and8_1_out_3, nand8_1_out_3, nor8_1_out_3, not8_1_out_2,
       or8_1_out_3, shifter1_1_out_3, shifter1_2_out_3, xor8_1_out_3;

  addsub addsub_1 (.C(Cin), .A(A), .B(B), .Sum(addsub_1_sum), .Sub(addsub_1_sub), .Co(Co));
  and8 and8_1 (.in_1(B), .in_2(A), .out_3(and8_1_out_3));
  or8 or8_1 (.in_1(B), .in_2(A), .out_3(or8_1_out_3));
  not8 not8_1 (.in_1(A), .out_2(not8_1_out_2));
  nor8 nor8_1 (.in_1(B), .in_2(A), .out_3(nor8_1_out_3));
  nand8 nand8_1 (.in_1(B), .in_2(A), .out_3(nand8_1_out_3));
  xor8 xor8_1 (.in_1(B), .in_2(A), .out_3(xor8_1_out_3));
  shifter1 shifter1_1 (.in_2(A), .out_3(shifter1_1_out_3));  // open: L
  shifter1 shifter1_2 (.L(1'b1), .in_2(A), .out_3(shifter1_2_out_3));
  mplex4d8 mplex4d8_1 (
    .S(Ctrl), .in_2(addsub_1_sum), .in_3(addsub_1_sub), .in_4(and8_1_out_3), .in_5(or8_1_out_3),
    .in_6(not8_1_out_2), .in_7(nor8_1_out_3), .in_8(nand8_1_out_3), .in_9(xor8_1_out_3),
    .in_10(shifter1_1_out_3), .in_11(shifter1_2_out_3), .out_18(out_5));  // open: in_12, in_13, in_14, in_15, in_16, in_17
endmodule

module addsub (
  input  C,
  input  [7:0] A,
  input  [7:0] B,
  output [7:0] Sum,
  output [7:0] Sub,
  output Co
);

  wire [7:0] comp2_1_out_2;

  add8cs add8cs_1 (.Ci(C), .A(A), .B(B), .out_4(Sum), .Co(Co));
  comp2 comp2_1 (.in_1(B), .out_2(comp2_1_out_2));
  add8cs add8cs_2 (.Ci(C), .A(A), .B(comp2_1_out_2), .out_4(Sub));  // open: Co
endmodule

module shifter1 (
  input  L,
  input  [7:0] in_2,
  output [7:0] out_3
);

  mplex1d8 mplex1d8_1 (.S(L), .in_2({in_2[6:0], 1'b0}), .in_3({1'b0, in_2[7:1]}), .out_4(out_3));
endmodule
