// Logisim project xor.circ as structural Verilog: 1 circuit, main circuit lab_xor
module lab_xor (
  input  in_1,
  input  in_2,
  output out_3
);

  wire and_1_out, and_2_out;

  and and_1 (and_1_out, ~in_1, in_2);  // AND_Gate
  and and_2 (and_2_out, in_1, ~in_2);  // AND_Gate
  or or_1 (out_3, and_1_out, and_2_out);
endmodule
